// Logisim project Computer.circ as structural Verilog: 6 circuits, main circuit main
module main (
);

  wire [3:0] clockunit_1_sys, txbcontrolgpr_1_rcb_a, txbcontrolgpr_1_rcb_b, txbcontrolgpr_1_rcb_c,
       txbcontrolgpr_1_rcb_d, txbcontrolgpr_1_rcb_e, txbcontrolgpr_1_rcb_f, txbcontrolgpr_1_rcb_fg,
       txbcontrolgpr_1_rcb_g, txbcontrolgpr_1_rcb_h, txbcontrolgpr_1_rcb_rs, txbcontrolgpr_1_rcb_th,
       txbcontrolgpr_1_rcb_tl, txbcontrolgpr_1_sys_out;
  wire [7:0] generalpurposeregister_1_mb, generalpurposeregister_1_txhb, generalpurposeregister_1_txlb,
       generalpurposeregister_9_data, generalpurposeregister_10_data;
  wire [10:0] undriven;

  ClockUnit clockunit_1 (.SYS(clockunit_1_sys));  // open: MANUAL_CLOCK, CLOCK_SELECT, CLOCK_OUT, INV_CLOCK_OUT
  TXBControlGPR txbcontrolgpr_1 (
    .SYS_IN(clockunit_1_sys), .TCTRLB(undriven), .SYS_OUT(txbcontrolgpr_1_sys_out),
    .RCB_A(txbcontrolgpr_1_rcb_a), .RCB_B(txbcontrolgpr_1_rcb_b), .RCB_C(txbcontrolgpr_1_rcb_c),
    .RCB_D(txbcontrolgpr_1_rcb_d), .RCB_E(txbcontrolgpr_1_rcb_e), .RCB_F(txbcontrolgpr_1_rcb_f),
    .RCB_G(txbcontrolgpr_1_rcb_g), .RCB_H(txbcontrolgpr_1_rcb_h), .RCB_TL(txbcontrolgpr_1_rcb_tl),
    .RCB_TH(txbcontrolgpr_1_rcb_th), .RCB_RS(txbcontrolgpr_1_rcb_rs), .RCB_FG(txbcontrolgpr_1_rcb_fg));  // open: out_14, out_15, out_16, out_17
  GeneralPurposeRegister generalpurposeregister_1 (
    .SYS(txbcontrolgpr_1_sys_out), .RCB(txbcontrolgpr_1_rcb_a), .TXLB(generalpurposeregister_1_txlb),
    .TXHB(generalpurposeregister_1_txhb), .MB(generalpurposeregister_1_mb));  // open: DATA
  GeneralPurposeRegister generalpurposeregister_2 (
    .SYS(txbcontrolgpr_1_sys_out), .RCB(txbcontrolgpr_1_rcb_b), .TXLB(generalpurposeregister_1_txlb),
    .TXHB(generalpurposeregister_1_txhb), .MB(generalpurposeregister_1_mb));  // open: DATA
  GeneralPurposeRegister generalpurposeregister_3 (
    .SYS(txbcontrolgpr_1_sys_out), .RCB(txbcontrolgpr_1_rcb_c), .TXLB(generalpurposeregister_1_txlb),
    .TXHB(generalpurposeregister_1_txhb), .MB(generalpurposeregister_1_mb));  // open: DATA
  GeneralPurposeRegister generalpurposeregister_4 (
    .SYS(txbcontrolgpr_1_sys_out), .RCB(txbcontrolgpr_1_rcb_d), .TXLB(generalpurposeregister_1_txlb),
    .TXHB(generalpurposeregister_1_txhb), .MB(generalpurposeregister_1_mb));  // open: DATA
  GeneralPurposeRegister generalpurposeregister_5 (
    .SYS(txbcontrolgpr_1_sys_out), .RCB(txbcontrolgpr_1_rcb_e), .TXLB(generalpurposeregister_1_txlb),
    .TXHB(generalpurposeregister_1_txhb), .MB(generalpurposeregister_1_mb));  // open: DATA
  GeneralPurposeRegister generalpurposeregister_6 (
    .SYS(txbcontrolgpr_1_sys_out), .RCB(txbcontrolgpr_1_rcb_f), .TXLB(generalpurposeregister_1_txlb),
    .TXHB(generalpurposeregister_1_txhb), .MB(generalpurposeregister_1_mb));  // open: DATA
  GeneralPurposeRegister generalpurposeregister_7 (
    .SYS(txbcontrolgpr_1_sys_out), .RCB(txbcontrolgpr_1_rcb_g), .TXLB(generalpurposeregister_1_txlb),
    .TXHB(generalpurposeregister_1_txhb), .MB(generalpurposeregister_1_mb));  // open: DATA
  GeneralPurposeRegister generalpurposeregister_8 (
    .SYS(txbcontrolgpr_1_sys_out), .RCB(txbcontrolgpr_1_rcb_h), .TXLB(generalpurposeregister_1_txlb),
    .TXHB(generalpurposeregister_1_txhb), .MB(generalpurposeregister_1_mb));  // open: DATA
  GeneralPurposeRegister generalpurposeregister_9 (
    .SYS(txbcontrolgpr_1_sys_out), .RCB(txbcontrolgpr_1_rcb_rs), .DATA(generalpurposeregister_9_data),
    .TXLB(generalpurposeregister_1_txlb), .TXHB(generalpurposeregister_1_txhb),
    .MB(generalpurposeregister_1_mb));
  GeneralPurposeRegister generalpurposeregister_10 (
    .SYS(txbcontrolgpr_1_sys_out), .RCB(txbcontrolgpr_1_rcb_fg), .DATA(generalpurposeregister_10_data),
    .TXLB(generalpurposeregister_1_txlb), .TXHB(generalpurposeregister_1_txhb),
    .MB(generalpurposeregister_1_mb));
  DecodeUnit decodeunit_1 ();  // open: INST_IN, INST_OUT
  Cache cache_1 ();  // open: SYS, READ, TXLB, TXHB

  // Notes on the sheet:
  //   GPR_A
  //   GPR_B
  //   GPR_C
  //   GPR_E
  //   GPR_F
  //   GPR_H
  //   GPR_D
  //   GPR_G
  //   RAM_SEL
  //   FLAGS
endmodule

module GeneralPurposeRegister (
  input  [3:0] RCB,
  input  [3:0] SYS,
  output [7:0] TXLB,
  output [7:0] TXHB,
  output [7:0] MB,
  output [7:0] DATA
);

  wire and_1_out, and_2_out, not_1_out, not_2_out, not_3_out, or_1_out;
  wire [7:0] controlled_buffer_1_out, controlled_buffer_3_out, controlled_buffer_5_out;

  Pull_Resistor pull_resistor_1 (.node(SYS[2]));
  not not_1 (not_1_out, RCB[1]);
  and and_1 (and_1_out, RCB[2], not_1_out);
  or or_1 (or_1_out, RCB[1], RCB[0]);
  and and_2 (and_2_out, not_1_out, RCB[3]);
  assign controlled_buffer_1_out = RCB[2] ? TXLB : 8'bz;  // Controlled_Buffer controlled_buffer_1
  assign controlled_buffer_1_out = RCB[3] ? TXHB : 8'bz;  // Controlled_Buffer controlled_buffer_2
  not not_2 (not_2_out, RCB[0]);
  assign controlled_buffer_3_out = RCB[0] ? {8{1'b1}} : 8'bz;  // Controlled_Buffer controlled_buffer_3
  assign controlled_buffer_3_out = not_2_out ? controlled_buffer_1_out : 8'bz;  // Controlled_Buffer controlled_buffer_4
  assign controlled_buffer_5_out = or_1_out ? controlled_buffer_3_out : 8'bz;  // Controlled_Buffer controlled_buffer_5
  not not_3 (not_3_out, SYS[1]);
  Register register_1 (.D(controlled_buffer_5_out), .en(or_1_out), .clk(not_3_out), .Q(DATA));  // open: clr
  assign TXHB = and_2_out ? DATA : 8'bz;  // Controlled_Buffer controlled_buffer_6
  assign TXLB = and_1_out ? DATA : 8'bz;  // Controlled_Buffer controlled_buffer_7

  assign MB = {8{1'b1}};
  // also tied to GND on the sheet: SYS[3]
  // also tied to VCC on the sheet: SYS[0]

  // Notes on the sheet:
  //   TXLB: pull=down
  //   TXHB: pull=down
  //   Transfer Bus (Lower)
  //   Transfer Bus (Higher)
  //   Main Bus
  //   Register Control Bus
  //   System Bus
endmodule

module ClockUnit (
  input  MANUAL_CLOCK,
  input  CLOCK_SELECT,
  output CLOCK_OUT,
  output INV_CLOCK_OUT,
  output [3:0] SYS
);

  wire and_1_out, and_2_out, clock_1_out, not_1_out;

  Clock clock_1 (.out(clock_1_out));
  not not_1 (not_1_out, CLOCK_SELECT);
  Pull_Resistor pull_resistor_1 (.node(CLOCK_SELECT));
  and and_1 (and_1_out, clock_1_out, not_1_out);
  and and_2 (and_2_out, MANUAL_CLOCK, CLOCK_SELECT);
  LED led_1 (.in(CLOCK_OUT));
  or or_1 (CLOCK_OUT, and_1_out, and_2_out);
  not not_2 (INV_CLOCK_OUT, CLOCK_OUT);
  Pull_Resistor #(.pull(1)) pull_resistor_2 (.node(SYS[2]));

  assign {SYS[3], SYS[1:0]} = {1'b0, CLOCK_OUT, 1'b1};
endmodule

module TXBControlGPR (
  input  [3:0] SYS_IN,
  input  [10:0] TCTRLB,
  output [3:0] SYS_OUT,
  output [3:0] RCB_A,
  output [3:0] RCB_B,
  output [3:0] RCB_C,
  output [3:0] RCB_D,
  output [3:0] RCB_E,
  output [3:0] RCB_F,
  output [3:0] RCB_G,
  output [3:0] RCB_H,
  output [3:0] RCB_TL,
  output [3:0] RCB_TH,
  output [3:0] out_14,
  output [3:0] out_15,
  output [3:0] out_16,
  output [3:0] out_17,
  output [3:0] RCB_RS,
  output [3:0] RCB_FG
);

  wire and_1_out, and_3_out, and_4_out, and_5_out, and_7_out, and_8_out, and_9_out, and_11_out, and_12_out,
       and_13_out, and_15_out, and_16_out, and_17_out, and_19_out, and_20_out, and_21_out, and_23_out,
       and_25_out, and_27_out, and_29_out, and_31_out, and_33_out, and_34_out, and_35_out, and_36_out,
       and_37_out, and_38_out, and_39_out, and_40_out, and_41_out, and_42_out, and_43_out, and_44_out,
       and_45_out, and_46_out, and_47_out, and_48_out, and_65_out, and_66_out, demultiplexer_1_out0,
       demultiplexer_1_out1, demultiplexer_1_out2, demultiplexer_1_out3, demultiplexer_1_out4,
       demultiplexer_1_out5, demultiplexer_1_out6, demultiplexer_1_out7, demultiplexer_2_out0,
       demultiplexer_2_out1, demultiplexer_2_out2, demultiplexer_2_out3, demultiplexer_2_out4,
       demultiplexer_2_out5, demultiplexer_2_out6, demultiplexer_2_out7, demultiplexer_2_out8,
       demultiplexer_2_out9, demultiplexer_2_out10, demultiplexer_2_out11, demultiplexer_2_out12,
       demultiplexer_2_out13, demultiplexer_2_out14, demultiplexer_2_out15, demultiplexer_3_out0,
       demultiplexer_3_out1, demultiplexer_3_out2, demultiplexer_3_out3, demultiplexer_3_out4,
       demultiplexer_3_out5, demultiplexer_3_out6, demultiplexer_3_out7, demultiplexer_3_out8,
       demultiplexer_3_out9, demultiplexer_3_out10, demultiplexer_3_out11, demultiplexer_3_out12,
       demultiplexer_3_out13, demultiplexer_3_out14, demultiplexer_3_out15, demultiplexer_4_out0,
       demultiplexer_4_out1, demultiplexer_4_out2, demultiplexer_4_out3, demultiplexer_4_out5,
       demultiplexer_5_out0, demultiplexer_5_out1, demultiplexer_5_out2, demultiplexer_5_out3,
       demultiplexer_5_out5, not_1_out, not_2_out, not_3_out, not_4_out, not_5_out, not_6_out, not_7_out,
       not_8_out, not_9_out, not_10_out, not_11_out, not_12_out, not_13_out, not_14_out, not_15_out,
       not_16_out, not_17_out, not_18_out, or_1_out, or_2_out, or_3_out, or_5_out, or_7_out, or_9_out,
       or_11_out, or_19_out, or_20_out, or_21_out, or_22_out, or_23_out, or_24_out, or_25_out, or_26_out,
       or_27_out, or_28_out, or_35_out, or_36_out, or_37_out, or_38_out, or_39_out, or_40_out, or_41_out,
       or_42_out, or_43_out, or_44_out, or_45_out, or_46_out;

  // NoConnect on SYS_IN[2]
  Demultiplexer #(.select(3)) demultiplexer_1 (
    .out0(demultiplexer_1_out0), .out1(demultiplexer_1_out1), .out2(demultiplexer_1_out2),
    .out3(demultiplexer_1_out3), .out4(demultiplexer_1_out4), .out5(demultiplexer_1_out5),
    .out6(demultiplexer_1_out6), .out7(demultiplexer_1_out7), .in(1'b1), .sel(TCTRLB[10:8]));
  or or_1 (or_1_out, demultiplexer_1_out6, demultiplexer_1_out5, demultiplexer_1_out3, demultiplexer_1_out1);
  Demultiplexer #(.select(4)) demultiplexer_2 (
    .out0(demultiplexer_2_out0), .out1(demultiplexer_2_out1), .out2(demultiplexer_2_out2),
    .out3(demultiplexer_2_out3), .out4(demultiplexer_2_out4), .out5(demultiplexer_2_out5),
    .out6(demultiplexer_2_out6), .out7(demultiplexer_2_out7), .out8(demultiplexer_2_out8),
    .out9(demultiplexer_2_out9), .out10(demultiplexer_2_out10), .out11(demultiplexer_2_out11),
    .out12(demultiplexer_2_out12), .out13(demultiplexer_2_out13), .out14(demultiplexer_2_out14),
    .out15(demultiplexer_2_out15), .in(or_1_out), .sel(TCTRLB[7:4]));
  or or_2 (or_2_out, demultiplexer_1_out5, demultiplexer_1_out1);
  Demultiplexer #(.select(4)) demultiplexer_3 (
    .out0(demultiplexer_3_out0), .out1(demultiplexer_3_out1), .out2(demultiplexer_3_out2),
    .out3(demultiplexer_3_out3), .out4(demultiplexer_3_out4), .out5(demultiplexer_3_out5),
    .out6(demultiplexer_3_out6), .out7(demultiplexer_3_out7), .out8(demultiplexer_3_out8),
    .out9(demultiplexer_3_out9), .out10(demultiplexer_3_out10), .out11(demultiplexer_3_out11),
    .out12(demultiplexer_3_out12), .out13(demultiplexer_3_out13), .out14(demultiplexer_3_out14),
    .out15(demultiplexer_3_out15), .in(or_2_out), .sel(TCTRLB[3:0]));
  and and_1 (and_1_out, demultiplexer_1_out1, demultiplexer_3_out0);
  or or_3 (or_3_out, and_1_out, demultiplexer_2_out0);
  and and_2 (RCB_A[3], demultiplexer_3_out0, not_1_out);
  not not_1 (not_1_out, demultiplexer_1_out1);
  and and_3 (and_3_out, demultiplexer_1_out1, demultiplexer_3_out1);
  or or_4 (RCB_B[2], and_3_out, demultiplexer_2_out1);
  and and_4 (and_4_out, demultiplexer_3_out1, not_2_out);
  not not_2 (not_2_out, demultiplexer_1_out1);
  and and_5 (and_5_out, demultiplexer_1_out1, demultiplexer_3_out2);
  or or_5 (or_5_out, and_5_out, demultiplexer_2_out2);
  and and_6 (RCB_C[3], demultiplexer_3_out2, not_3_out);
  not not_3 (not_3_out, demultiplexer_1_out1);
  and and_7 (and_7_out, demultiplexer_1_out1, demultiplexer_3_out3);
  or or_6 (RCB_D[2], and_7_out, demultiplexer_2_out3);
  and and_8 (and_8_out, demultiplexer_3_out3, not_4_out);
  not not_4 (not_4_out, demultiplexer_1_out1);
  and and_9 (and_9_out, demultiplexer_1_out1, demultiplexer_3_out4);
  or or_7 (or_7_out, and_9_out, demultiplexer_2_out4);
  and and_10 (RCB_E[3], demultiplexer_3_out4, not_5_out);
  not not_5 (not_5_out, demultiplexer_1_out1);
  and and_11 (and_11_out, demultiplexer_1_out1, demultiplexer_3_out5);
  or or_8 (RCB_F[2], and_11_out, demultiplexer_2_out5);
  and and_12 (and_12_out, demultiplexer_3_out5, not_6_out);
  not not_6 (not_6_out, demultiplexer_1_out1);
  and and_13 (and_13_out, demultiplexer_1_out1, demultiplexer_3_out6);
  or or_9 (or_9_out, and_13_out, demultiplexer_2_out6);
  and and_14 (RCB_G[3], demultiplexer_3_out6, not_7_out);
  not not_7 (not_7_out, demultiplexer_1_out1);
  and and_15 (and_15_out, demultiplexer_1_out1, demultiplexer_3_out7);
  or or_10 (RCB_H[2], and_15_out, demultiplexer_2_out7);
  and and_16 (and_16_out, demultiplexer_3_out7, not_8_out);
  not not_8 (not_8_out, demultiplexer_1_out1);
  and and_17 (and_17_out, demultiplexer_1_out1, demultiplexer_3_out8);
  or or_11 (or_11_out, and_17_out, demultiplexer_2_out8);
  and and_18 (RCB_TL[3], demultiplexer_3_out8, not_9_out);
  not not_9 (not_9_out, demultiplexer_1_out1);
  and and_19 (and_19_out, demultiplexer_1_out1, demultiplexer_3_out9);
  or or_12 (RCB_TH[2], and_19_out, demultiplexer_2_out9);
  and and_20 (and_20_out, demultiplexer_3_out9, not_10_out);
  not not_10 (not_10_out, demultiplexer_1_out1);
  and and_21 (and_21_out, demultiplexer_1_out1, demultiplexer_3_out10);
  or or_13 (out_14[2], and_21_out, demultiplexer_2_out10);
  and and_22 (out_14[3], demultiplexer_3_out10, not_11_out);
  not not_11 (not_11_out, demultiplexer_1_out1);
  and and_23 (and_23_out, demultiplexer_1_out1, demultiplexer_3_out11);
  or or_14 (out_15[2], and_23_out, demultiplexer_2_out11);
  and and_24 (out_15[3], demultiplexer_3_out11, not_12_out);
  not not_12 (not_12_out, demultiplexer_1_out1);
  and and_25 (and_25_out, demultiplexer_1_out1, demultiplexer_3_out12);
  or or_15 (out_16[2], and_25_out, demultiplexer_2_out12);
  and and_26 (out_16[3], demultiplexer_3_out12, not_13_out);
  not not_13 (not_13_out, demultiplexer_1_out1);
  and and_27 (and_27_out, demultiplexer_1_out1, demultiplexer_3_out13);
  or or_16 (out_17[2], and_27_out, demultiplexer_2_out13);
  and and_28 (out_17[3], demultiplexer_3_out13, not_14_out);
  not not_14 (not_14_out, demultiplexer_1_out1);
  and and_29 (and_29_out, demultiplexer_1_out1, demultiplexer_3_out14);
  or or_17 (RCB_RS[2], and_29_out, demultiplexer_2_out14);
  and and_30 (RCB_RS[3], demultiplexer_3_out14, not_15_out);
  not not_15 (not_15_out, demultiplexer_1_out1);
  and and_31 (and_31_out, demultiplexer_1_out1, demultiplexer_3_out15);
  or or_18 (RCB_FG[2], and_31_out, demultiplexer_2_out15);
  and and_32 (RCB_FG[3], demultiplexer_3_out15, not_16_out);
  not not_16 (not_16_out, demultiplexer_1_out1);
  and and_33 (and_33_out, demultiplexer_1_out6, demultiplexer_2_out0);
  and and_34 (and_34_out, demultiplexer_1_out6, demultiplexer_2_out1);
  and and_35 (and_35_out, demultiplexer_1_out6, demultiplexer_2_out2);
  and and_36 (and_36_out, demultiplexer_1_out6, demultiplexer_2_out3);
  and and_37 (and_37_out, demultiplexer_1_out6, demultiplexer_2_out4);
  and and_38 (and_38_out, demultiplexer_1_out6, demultiplexer_2_out5);
  and and_39 (and_39_out, demultiplexer_1_out6, demultiplexer_2_out6);
  and and_40 (and_40_out, demultiplexer_1_out6, demultiplexer_2_out7);
  and and_41 (and_41_out, demultiplexer_1_out6, demultiplexer_2_out8);
  and and_42 (and_42_out, demultiplexer_1_out6, demultiplexer_2_out9);
  and and_43 (and_43_out, demultiplexer_1_out6, demultiplexer_2_out10);
  and and_44 (and_44_out, demultiplexer_1_out6, demultiplexer_2_out11);
  and and_45 (and_45_out, demultiplexer_1_out6, demultiplexer_2_out12);
  and and_46 (and_46_out, demultiplexer_1_out6, demultiplexer_2_out13);
  and and_47 (and_47_out, demultiplexer_1_out6, demultiplexer_2_out14);
  and and_48 (and_48_out, demultiplexer_1_out6, demultiplexer_2_out15);
  or or_19 (or_19_out, and_33_out, and_1_out);
  and and_49 (RCB_A[0], demultiplexer_1_out5, or_3_out);
  or or_20 (or_20_out, and_34_out, and_3_out);
  and and_50 (RCB_B[0], demultiplexer_1_out5, RCB_B[2]);
  or or_21 (or_21_out, and_35_out, and_5_out);
  and and_51 (RCB_C[0], demultiplexer_1_out5, or_5_out);
  or or_22 (or_22_out, and_36_out, and_7_out);
  and and_52 (RCB_D[0], demultiplexer_1_out5, RCB_D[2]);
  or or_23 (or_23_out, and_37_out, and_9_out);
  and and_53 (RCB_E[0], demultiplexer_1_out5, or_7_out);
  or or_24 (or_24_out, and_38_out, and_11_out);
  and and_54 (RCB_F[0], demultiplexer_1_out5, RCB_F[2]);
  or or_25 (or_25_out, and_39_out, and_13_out);
  and and_55 (RCB_G[0], demultiplexer_1_out5, or_9_out);
  or or_26 (or_26_out, and_40_out, and_15_out);
  and and_56 (RCB_H[0], demultiplexer_1_out5, RCB_H[2]);
  or or_27 (or_27_out, and_41_out, and_17_out);
  and and_57 (RCB_TL[0], demultiplexer_1_out5, or_11_out);
  or or_28 (or_28_out, and_42_out, and_19_out);
  and and_58 (RCB_TH[0], demultiplexer_1_out5, RCB_TH[2]);
  or or_29 (out_14[1], and_43_out, and_21_out);
  and and_59 (out_14[0], demultiplexer_1_out5, out_14[2]);
  or or_30 (out_15[1], and_44_out, and_23_out);
  and and_60 (out_15[0], demultiplexer_1_out5, out_15[2]);
  or or_31 (out_16[1], and_45_out, and_25_out);
  and and_61 (out_16[0], demultiplexer_1_out5, out_16[2]);
  or or_32 (out_17[1], and_46_out, and_27_out);
  and and_62 (out_17[0], demultiplexer_1_out5, out_17[2]);
  or or_33 (RCB_RS[1], and_47_out, and_29_out);
  and and_63 (RCB_RS[0], demultiplexer_1_out5, RCB_RS[2]);
  or or_34 (RCB_FG[1], and_48_out, and_31_out);
  and and_64 (RCB_FG[0], demultiplexer_1_out5, RCB_FG[2]);
  or or_35 (or_35_out, demultiplexer_1_out2, demultiplexer_1_out4);
  not not_17 (not_17_out, TCTRLB[7]);
  and and_65 (and_65_out, not_17_out, or_35_out);
  Demultiplexer #(.select(3)) demultiplexer_4 (
    .out0(demultiplexer_4_out0), .out1(demultiplexer_4_out1), .out2(demultiplexer_4_out2),
    .out3(demultiplexer_4_out3), .out5(demultiplexer_4_out5), .in(and_65_out), .sel(TCTRLB[6:4]));  // open: out4, out6, out7
  not not_18 (not_18_out, TCTRLB[3]);
  or or_36 (or_36_out, demultiplexer_1_out2, demultiplexer_1_out7);
  and and_66 (and_66_out, not_18_out, or_36_out);
  Demultiplexer #(.select(3)) demultiplexer_5 (
    .out0(demultiplexer_5_out0), .out1(demultiplexer_5_out1), .out2(demultiplexer_5_out2),
    .out3(demultiplexer_5_out3), .out5(demultiplexer_5_out5), .in(and_66_out), .sel(TCTRLB[2:0]));  // open: out4, out6, out7
  or or_37 (or_37_out, demultiplexer_5_out0, demultiplexer_4_out0);
  or or_38 (or_38_out, demultiplexer_5_out0, demultiplexer_4_out0);
  or or_39 (or_39_out, demultiplexer_5_out1, demultiplexer_4_out1);
  or or_40 (or_40_out, demultiplexer_5_out1, demultiplexer_4_out1);
  or or_41 (or_41_out, demultiplexer_5_out2, demultiplexer_4_out2);
  or or_42 (or_42_out, demultiplexer_5_out2, demultiplexer_4_out2);
  or or_43 (or_43_out, demultiplexer_5_out3, demultiplexer_4_out3);
  or or_44 (or_44_out, demultiplexer_5_out3, demultiplexer_4_out3);
  or or_45 (or_45_out, demultiplexer_5_out5, demultiplexer_4_out5);
  or or_46 (or_46_out, demultiplexer_5_out5, demultiplexer_4_out5);
  or or_47 (RCB_A[1], demultiplexer_5_out0, or_19_out);
  or or_48 (RCB_B[1], demultiplexer_5_out0, or_20_out);
  or or_49 (RCB_C[1], demultiplexer_5_out1, or_21_out);
  or or_50 (RCB_D[1], demultiplexer_5_out1, or_22_out);
  or or_51 (RCB_E[1], demultiplexer_5_out2, or_23_out);
  or or_52 (RCB_F[1], demultiplexer_5_out2, or_24_out);
  or or_53 (RCB_G[1], demultiplexer_5_out3, or_25_out);
  or or_54 (RCB_H[1], demultiplexer_5_out3, or_26_out);
  or or_55 (RCB_TL[1], demultiplexer_5_out5, or_27_out);
  or or_56 (RCB_TH[1], demultiplexer_5_out5, or_28_out);
  or or_57 (RCB_A[2], or_37_out, or_3_out);
  or or_58 (RCB_B[3], or_38_out, and_4_out);
  or or_59 (RCB_C[2], or_39_out, or_5_out);
  or or_60 (RCB_D[3], or_40_out, and_8_out);
  or or_61 (RCB_E[2], or_41_out, or_7_out);
  or or_62 (RCB_F[3], or_42_out, and_12_out);
  or or_63 (RCB_G[2], or_43_out, or_9_out);
  or or_64 (RCB_H[3], or_44_out, and_16_out);
  or or_65 (RCB_TL[2], or_45_out, or_11_out);
  or or_66 (RCB_TH[3], or_46_out, and_20_out);

  assign SYS_OUT = {SYS_IN[3], 1'b1, SYS_IN[1:0]};
endmodule

module DecodeUnit (
  input  [15:0] INST_IN,
  output [7:0] INST_OUT
);

  wire and_1_out, and_2_out, and_3_out, and_4_out, and_5_out, and_6_out, and_7_out, and_8_out, and_9_out,
       and_10_out, and_11_out, not_1_out, not_2_out, not_3_out, not_4_out, not_5_out, not_6_out, not_7_out,
       not_8_out, not_9_out, not_10_out, not_11_out, or_1_out, or_2_out, or_3_out, or_4_out, or_5_out;

  or or_1 (or_1_out, INST_IN[15], INST_IN[14], INST_IN[13], INST_IN[12]);
  not not_1 (not_1_out, or_1_out);
  or or_2 (or_2_out, INST_IN[11], INST_IN[10], INST_IN[9], INST_IN[8]);
  or or_3 (or_3_out, INST_IN[7], INST_IN[6], INST_IN[5], INST_IN[4]);
  and and_1 (and_1_out, not_1_out, not_2_out);
  not not_2 (not_2_out, and_2_out);
  not not_3 (not_3_out, and_3_out);
  and and_2 (and_2_out, not_1_out, or_2_out);
  and and_3 (and_3_out, and_1_out, or_3_out);
  or or_4 (or_4_out, INST_IN[3], INST_IN[2], INST_IN[1], INST_IN[0]);
  and and_4 (and_4_out, and_1_out, not_3_out);
  not not_4 (not_4_out, and_5_out);
  and and_5 (and_5_out, and_4_out, or_4_out);
  and and_6 (and_6_out, and_4_out, not_4_out);
  or or_5 (or_5_out, and_6_out, and_5_out, and_3_out);
  not not_5 (not_5_out, INST_IN[6]);
  not not_6 (not_6_out, INST_IN[7]);
  Pull_Resistor pull_resistor_1 (.node(INST_OUT[3:0]));
  Pull_Resistor pull_resistor_2 (.node(INST_OUT[7:4]));
  assign INST_OUT[3:0] = and_7_out ? INST_IN[3:0] : 4'bz;  // Controlled_Buffer controlled_buffer_1
  assign INST_OUT[7:4] = and_7_out ? INST_IN[7:4] : 4'bz;  // Controlled_Buffer controlled_buffer_2
  and and_7 (and_7_out, or_5_out, and_8_out);
  and and_8 (and_8_out, not_5_out, not_6_out);
  assign INST_OUT[3:0] = and_9_out ? INST_IN[7:4] : 4'bz;  // Controlled_Buffer controlled_buffer_3
  assign INST_OUT[7:4] = and_9_out ? 4'b0100 : 4'bz;  // Controlled_Buffer controlled_buffer_4
  assign INST_OUT[3:0] = and_11_out ? INST_IN[7:4] : 4'bz;  // Controlled_Buffer controlled_buffer_5
  and and_9 (and_9_out, not_7_out, or_5_out);
  not not_7 (not_7_out, and_8_out);
  not not_8 (not_8_out, INST_IN[9]);
  not not_9 (not_9_out, INST_IN[10]);
  not not_10 (not_10_out, INST_IN[11]);
  assign INST_OUT[3:0] = and_10_out ? INST_IN[11:8] : 4'bz;  // Controlled_Buffer controlled_buffer_6
  assign INST_OUT[7:4] = and_11_out ? 4'b0101 : 4'bz;  // Controlled_Buffer controlled_buffer_7
  and and_10 (and_10_out, not_11_out, and_2_out);
  and and_11 (and_11_out, INST_IN[8], not_8_out, not_9_out, not_10_out, and_2_out);
  not not_11 (not_11_out, and_11_out);
  assign INST_OUT[7:4] = and_10_out ? 4'b0110 : 4'bz;  // Controlled_Buffer controlled_buffer_8
  assign INST_OUT[3:0] = or_1_out ? INST_IN[15:12] : 4'bz;  // Controlled_Buffer controlled_buffer_9
  assign INST_OUT[7:4] = or_1_out ? 4'b0111 : 4'bz;  // Controlled_Buffer controlled_buffer_10
endmodule

module Cache (
  input  [3:0] SYS,
  input  READ,
  output [7:0] TXLB,
  output [7:0] TXHB
);

  wire and_1_out, and_2_out, not_1_out;
  wire [7:0] controlled_buffer_1_out, ram_1_dout;

  and and_1 (and_1_out, SYS[1], SYS[2]);
  and and_2 (and_2_out, SYS[2], not_1_out);
  not not_1 (not_1_out, READ);
  assign controlled_buffer_1_out = and_2_out ? TXLB : 8'bz;  // Controlled_Buffer controlled_buffer_1
  Pull_Resistor pull_resistor_1 (.node(controlled_buffer_1_out));
  Pull_Resistor pull_resistor_2 (.node(TXHB));
  RAM ram_1 (.addr(TXHB), .we(and_2_out), .oe(1'b1), .clk(and_1_out), .din(controlled_buffer_1_out), .dout(ram_1_dout));
  assign TXLB = READ ? ram_1_dout : 8'bz;  // Controlled_Buffer controlled_buffer_2
  // also tied to GND on the sheet: SYS[3]
  // also tied to VCC on the sheet: SYS[0]
endmodule
